# Fritzing sketch Tp2 (saved by Fritzing 1.0.3b)
breadboards: 1

parts:
  Mod1 = Raspberry Pi Pico W
  Part1 = KY-037 High Sensitivity Sound Detection Module [package="Breakout board"]
  R1 = Resistor [tolerance=±5% power=0.25W resistance=220 package=THT]
  R2 = Resistor [tolerance=±5% power=0.25W resistance=220 package=THT]
  DI1 = 7-Segment LED Display [package=THT]
  LED1 = LED - 5mm [color="Red (633nm)" current=0.030A package="5 mm [THT]"]
  LED2 = LED - 5mm [color="Red (633nm)" current=0.030A package="5 mm [THT]"]
  R3 = Resistor [tolerance=±5% power=0.25W resistance=220 package=THT]
  R4 = Resistor [tolerance=±5% power=0.25W resistance=220 package=THT]

nets:
  N1: Mod1.pin_3, Mod1.pin_8, Mod1.pin_13, Mod1.pin_18, Mod1.pin_23, Mod1.pin_28, Mod1.pin_33, Mod1.pin_38, DI1.commAnode#2
  N2: Mod1.pin_15, R2.Pin_1
  N3: Mod1.pin_16, R4.Pin_1
  N4: Mod1.pin_19, R1.Pin_1
  N5: Mod1.pin_20, R3.Pin_1
  N6: Mod1.pin_34, Part1.A0
  N7: Mod1.pin_36, Part1.+
  N8: Part1.G, LED1.cathode, LED2.cathode
  N9: R1.Pin_0, DI1.cathodeD
  N10: R2.Pin_0, LED1.anode
  N11: DI1.cathodeE, R3.Pin_0
  N12: LED2.anode, R4.Pin_0

custom parts:
  Raspberry Pi Pico W: Raspberry Pi Pico W. Based around the RP2040 microcontroller the Pico W is a low cost microcontroller device bringing Raspberry Pi quality, cost, and easy of use to the microcontroller space. The areas marked KEEPOUT in pcb silkscreen should not have traces running through them to avoid shorts on a soldered in module!
  KY-037 High Sensitivity Sound Detection Module: KY-037 high sensitivity sound detection module is an analog/digital sensor that uses a condenser microphone to observe changes in environment noise.
